# Fritzing sketch BluetoothDemo (saved by Fritzing 0.9.1b)
breadboards: 1

parts:
  Componente1 = Arduino Uno (Rev3)
  Componente2 = Bluetooth HC-05 Macho

nets:
  5V: Componente1.5V, Componente2.VCC
  GND: Componente1.GND, Componente2.GND
