# Fritzing sketch DHT22 (saved by Fritzing 0.9.0b)
circuit board: 4.96712cm x 4.39326cm
breadboards: 1

parts:
  Sensor_Reading = DHT22 Humidity and Temperature Sensor
  Arduino_Nano = Arduino Nano (Rev3.0)

nets:
  VDD: Sensor_Reading.VDD, Arduino_Nano.5V
  N1: Sensor_Reading.DATA, Arduino_Nano.D2
  GND: Sensor_Reading.GND, Arduino_Nano.GND

notes:
  Using DHT22 breakout with 5.1k pullup resistor
